# Fritzing sketch Light Intensity Measurement Tool with LDR Based on Arduino UNO (saved by Fritzing 0.9.2b)
breadboards: 1

parts:
  LCD1 = LCD screen
  Part1 = Arduino Uno (Rev3)
  R1 = Rotary Potentiometer (Large) [maximum_resistance=100kΩ package=THT]
  R2 = Resistor [tolerance=±5% resistance=220 package=THT]
  R3 = Photocell (LDR) [package=THT]
  R4 = Resistor [tolerance=±5% resistance=220 package=THT]

nets:
  VSS: LCD1.VSS, LCD1.R/W, LCD1.LED-, Part1.GND, R1.leg1, R4.Pin_0
  VDD: LCD1.VDD, Part1.5V, R1.leg2, R2.Pin_1, R3.pin_1
  N1: LCD1.V0, R1.wiper
  N2: LCD1.RS, Part1.D12/MISO
  N3: LCD1.E, Part1.D11_PWM/MOSI
  N4: LCD1.DB4, Part1.D7
  N5: LCD1.DB5, Part1.D6_PWM
  N6: LCD1.DB6, Part1.D5_PWM
  N7: LCD1.DB7, Part1.D4
  N8: LCD1.LED+, R2.Pin_0
  N9: Part1.A0, R3.pin_0
